# Fritzing sketch ac_power_monitoring_wiring (saved by Fritzing 0.9.3b)
breadboards: 1

parts:
  M1 = Arduino Mega 2560+wifi R3
  Part1 = Voltage Sensor Module
  Part2 = Voltage Sensor Module
  Part3 = Voltage Sensor Module
  Part4 = ACS712 Current Sensor Module
  Part5 = ACS712 Current Sensor Module
  Part6 = ACS712 Current Sensor Module
  U1 = Module 4 Relais 5V [package="Module 4 Relais 5V"]

nets:
  N1: M1.A0, Part1.OUT
  N2: M1.A1, Part2.OUT
  N3: M1.A2, Part3.OUT
  N4: M1.A3, Part4.OUT
  N5: M1.A4, Part5.OUT
  N6: M1.A5, Part6.OUT
  N7: M1.D0_RX0, M1.TXD
  N8: M1.D1_TX0, M1.RXD
  N9: M1.D2_PWM, U1.IN1
  N10: M1.D3_PWM, U1.IN2
  N11: M1.D4_PWM, U1.IN3
  N12: M1.D5_PWM, U1.IN4
  VCC: M1.5V, M1.ICSP_5V, Part1.VCC, Part2.VCC, Part3.VCC, Part4.VCC, Part5.VCC, Part6.VCC, U1.VCC
  GND: M1.GND, M1.ICSP_GND, Part1.GND, Part2.GND, Part3.GND, Part4.GND, Part5.GND, Part6.GND, U1.GND

notes:
  Current sensor
  Voltage sensor
  4 Channel Relays

custom parts:
  Arduino Mega 2560+wifi R3: Generic Arduino Mega 2560+wifi R3 board.
  Module 4 Relais 5V: Module 4 Relais 5V 4x SPD-06VDC-SD-C
